// Logisim project FSM.circ as structural Verilog
module fsm (
  input  [1:0] in,
  input  clk,
  input  clr,
  output out_4
);

  wire reset;
  wire [1:0] multiplexer_1_out, register_2_q, run_1_out_3;

  Register #(.width(1)) register_1 (.D(clr), .Q(reset), .clk(clk));  // open: en, clr
  run run_1 (.in(in), .state(register_2_q), .out_3(run_1_out_3));
  Multiplexer #(.width(2), .enable("false")) multiplexer_1 (
    .in0(run_1_out_3), .in1(2'b00), .out(multiplexer_1_out), .sel(reset));
  Comparator #(.width(2)) comparator_1 (.a(2'b11), .b(multiplexer_1_out), .eq(out_4));  // open: gt, lt
  Register #(.width(2)) register_2 (.D(run_1_out_3), .Q(register_2_q), .clk(clk), .clr(reset));  // open: en
endmodule

module run (
  input  [1:0] in,
  input  [1:0] state,
  output [1:0] out_3
);

  wire [1:0] multiplexer_1_out, multiplexer_2_out, multiplexer_3_out, multiplexer_4_out;

  Multiplexer #(.select(2), .width(2), .enable("false")) multiplexer_1 (
    .in0(2'b00), .in1(2'b01), .in2(2'b00), .in3(2'b00), .out(multiplexer_1_out), .sel(in));
  Multiplexer #(.select(2), .width(2), .enable("false")) multiplexer_2 (
    .in0(2'b10), .in1(2'b01), .in2(2'b10), .in3(2'b00), .out(multiplexer_2_out), .sel(in));
  Multiplexer #(.select(2), .width(2), .enable("false")) multiplexer_3 (
    .in0(2'b11), .in1(2'b01), .in2(2'b11), .in3(2'b00), .out(multiplexer_3_out), .sel(in));
  Multiplexer #(.select(2), .width(2), .enable("false")) multiplexer_4 (
    .in0(2'b00), .in1(2'b01), .in2(2'b00), .in3(2'b00), .out(multiplexer_4_out), .sel(in));
  Multiplexer #(.select(2), .width(2), .enable("false")) multiplexer_5 (
    .in0(multiplexer_1_out), .in1(multiplexer_2_out), .in2(multiplexer_3_out), .in3(multiplexer_4_out),
    .out(out_3), .sel(state));
endmodule
