// Logisim project GRF.circ as structural Verilog: 7 circuits, main circuit grf
module grf (
  input  clk,
  input  reset,
  input  WE,
  input  [4:0] A1,
  input  [4:0] A2,
  input  [4:0] A3,
  input  [31:0] WD,
  output [31:0] RD1,
  output [31:0] RD2
);

  wire comparator_1_eq;
  wire [31:0] multiplexer_1_out;

  Comparator #(.width(5)) comparator_1 (.a(A3), .b({5{1'b0}}), .eq(comparator_1_eq));  // open: gt, lt
  Multiplexer #(.width(32)) multiplexer_1 (
    .in0(WD), .in1({32{1'b0}}), .out(multiplexer_1_out), .sel(comparator_1_eq));  // open: en
  L5 l5_1 (
    .in_1(A1), .in_3(A2), .in_4(A3), .in_7(multiplexer_1_out), .in_5(clk), .in_2(WE), .in_6(reset),
    .out_8(RD1), .out_9(RD2));
endmodule

module L4 (
  input  [3:0] in_1,
  input  in_2,
  input  [3:0] in_3,
  input  [3:0] in_4,
  input  in_5,
  input  in_6,
  input  [31:0] in_7,
  output [31:0] out_8,
  output [31:0] out_9
);

  wire E0, E1, not_1_out;
  wire [31:0] l3_1_out_8, l3_1_out_9, l3_2_out_8, l3_2_out_9;

  and and_1 (E0, in_2, not_1_out);
  not not_1 (not_1_out, in_4[3]);
  and and_2 (E1, in_2, in_4[3]);
  L3 l3_1 (
    .in_1(in_1[2:0]), .in_3(in_3[2:0]), .in_4(in_4[2:0]), .in_7(in_7), .in_5(in_5), .in_2(E0), .in_6(in_6),
    .out_8(l3_1_out_8), .out_9(l3_1_out_9));
  L3 l3_2 (
    .in_1(in_1[2:0]), .in_3(in_3[2:0]), .in_4(in_4[2:0]), .in_7(in_7), .in_5(in_5), .in_2(E1), .in_6(in_6),
    .out_8(l3_2_out_8), .out_9(l3_2_out_9));
  Multiplexer #(.width(32)) multiplexer_1 (.in0(l3_1_out_8), .in1(l3_2_out_8), .out(out_8), .sel(in_1[3]));  // open: en
  Multiplexer #(.width(32)) multiplexer_2 (.in0(l3_1_out_9), .in1(l3_2_out_9), .out(out_9), .sel(in_3[3]));  // open: en

  // Other names for the same wires on the sheet: T1[2:0] = in_1[2:0]; S1 = in_1[3]; T2[2:0] = in_3[2:0]; S2 = in_3[3];
  //   T3[2:0] = in_4[2:0]
endmodule

module L3 (
  input  [2:0] in_1,
  input  in_2,
  input  [2:0] in_3,
  input  [2:0] in_4,
  input  in_5,
  input  in_6,
  input  [31:0] in_7,
  output [31:0] out_8,
  output [31:0] out_9
);

  wire E0, E1, not_1_out;
  wire [31:0] l2_1_out_8, l2_1_out_9, l2_2_out_8, l2_2_out_9;

  and and_1 (E0, in_2, not_1_out);
  not not_1 (not_1_out, in_4[2]);
  and and_2 (E1, in_2, in_4[2]);
  L2 l2_1 (
    .in_1(in_1[1:0]), .in_3(in_3[1:0]), .in_4(in_4[1:0]), .in_7(in_7), .in_5(in_5), .in_2(E0), .in_6(in_6),
    .out_8(l2_1_out_8), .out_9(l2_1_out_9));
  L2 l2_2 (
    .in_1(in_1[1:0]), .in_3(in_3[1:0]), .in_4(in_4[1:0]), .in_7(in_7), .in_5(in_5), .in_2(E1), .in_6(in_6),
    .out_8(l2_2_out_8), .out_9(l2_2_out_9));
  Multiplexer #(.width(32)) multiplexer_1 (.in0(l2_1_out_8), .in1(l2_2_out_8), .out(out_8), .sel(in_1[2]));  // open: en
  Multiplexer #(.width(32)) multiplexer_2 (.in0(l2_1_out_9), .in1(l2_2_out_9), .out(out_9), .sel(in_3[2]));  // open: en

  // Other names for the same wires on the sheet: T1[1:0] = in_1[1:0]; S1 = in_1[2]; T2[1:0] = in_3[1:0]; S2 = in_3[2];
  //   T3[1:0] = in_4[1:0]
endmodule

module L2 (
  input  [1:0] in_1,
  input  in_2,
  input  [1:0] in_3,
  input  [1:0] in_4,
  input  in_5,
  input  in_6,
  input  [31:0] in_7,
  output [31:0] out_8,
  output [31:0] out_9
);

  wire E0, E1, not_1_out;
  wire [31:0] l1_1_out_8, l1_1_out_9, l1_2_out_8, l1_2_out_9;

  and and_1 (E0, in_2, not_1_out);
  not not_1 (not_1_out, in_4[1]);
  and and_2 (E1, in_2, in_4[1]);
  L1 l1_1 (
    .in_2(in_1[0]), .in_3(in_3[0]), .in_4(in_4[0]), .in_7(in_7), .in_5(in_5), .in_1(E0), .in_6(in_6),
    .out_8(l1_1_out_8), .out_9(l1_1_out_9));
  L1 l1_2 (
    .in_2(in_1[0]), .in_3(in_3[0]), .in_4(in_4[0]), .in_7(in_7), .in_5(in_5), .in_1(E1), .in_6(in_6),
    .out_8(l1_2_out_8), .out_9(l1_2_out_9));
  Multiplexer #(.width(32)) multiplexer_1 (.in0(l1_1_out_8), .in1(l1_2_out_8), .out(out_8), .sel(in_1[1]));  // open: en
  Multiplexer #(.width(32)) multiplexer_2 (.in0(l1_1_out_9), .in1(l1_2_out_9), .out(out_9), .sel(in_3[1]));  // open: en

  // Other names for the same wires on the sheet: T1 = in_1[0]; S1 = in_1[1]; T2 = in_3[0]; S2 = in_3[1]; T3 = in_4[0]
endmodule

module L1 (
  input  in_1,
  input  in_2,
  input  in_3,
  input  in_4,
  input  in_5,
  input  in_6,
  input  [31:0] in_7,
  output [31:0] out_8,
  output [31:0] out_9
);

  wire E0, E1, not_1_out;
  wire [31:0] l0_1_out_5, l0_2_out_5;

  not not_1 (not_1_out, in_4);
  L0 l0_1 (.in_4(in_7), .in_1(in_5), .in_2(E0), .in_3(in_6), .out_5(l0_1_out_5));
  L0 l0_2 (.in_4(in_7), .in_1(in_5), .in_2(E1), .in_3(in_6), .out_5(l0_2_out_5));
  and and_1 (E0, in_1, not_1_out);
  and and_2 (E1, in_1, in_4);
  Multiplexer #(.width(32)) multiplexer_1 (.in0(l0_1_out_5), .in1(l0_2_out_5), .out(out_8), .sel(in_2));  // open: en
  Multiplexer #(.width(32)) multiplexer_2 (.in0(l0_1_out_5), .in1(l0_2_out_5), .out(out_9), .sel(in_3));  // open: en

  // Other names for the same wires on the sheet: S1 = in_2; S2 = in_3
endmodule

module L0 (
  input  in_1,
  input  in_2,
  input  in_3,
  input  [31:0] in_4,
  output [31:0] out_5
);

  Register #(.width(32)) register_1 (.D(in_4), .en(in_2), .Q(out_5), .clk(in_1), .clr(in_3));
endmodule

module L5 (
  input  [4:0] in_1,
  input  in_2,
  input  [4:0] in_3,
  input  [4:0] in_4,
  input  in_5,
  input  in_6,
  input  [31:0] in_7,
  output [31:0] out_8,
  output [31:0] out_9
);

  wire E0, E1, not_1_out;
  wire [31:0] l4_1_out_8, l4_1_out_9, l4_2_out_8, l4_2_out_9;

  and and_1 (E0, in_2, not_1_out);
  not not_1 (not_1_out, in_4[4]);
  and and_2 (E1, in_2, in_4[4]);
  L4 l4_1 (
    .in_1(in_1[3:0]), .in_3(in_3[3:0]), .in_4(in_4[3:0]), .in_7(in_7), .in_5(in_5), .in_2(E0), .in_6(in_6),
    .out_8(l4_1_out_8), .out_9(l4_1_out_9));
  L4 l4_2 (
    .in_1(in_1[3:0]), .in_3(in_3[3:0]), .in_4(in_4[3:0]), .in_7(in_7), .in_5(in_5), .in_2(E1), .in_6(in_6),
    .out_8(l4_2_out_8), .out_9(l4_2_out_9));
  Multiplexer #(.width(32)) multiplexer_1 (.in0(l4_1_out_8), .in1(l4_2_out_8), .out(out_8), .sel(in_1[4]));  // open: en
  Multiplexer #(.width(32)) multiplexer_2 (.in0(l4_1_out_9), .in1(l4_2_out_9), .out(out_9), .sel(in_3[4]));  // open: en

  // Other names for the same wires on the sheet: T1[3:0] = in_1[3:0]; S1 = in_1[4]; T2[3:0] = in_3[3:0]; S2 = in_3[4];
  //   T3[3:0] = in_4[3:0]
endmodule
