// Logisim project ftoi.circ as structural Verilog
module ftoi (
  input  [15:0] in_1,
  output [31:0] out_2
);

  wire comparator_1_eq, comparator_2_gt, or_2_out;
  wire [4:0] subtractor_1_out;
  wire [31:0] neg_1_out_3, or_1_out, shifter_1_out, shifter_2_out, shifter_3_out;

  Subtractor #(.width(5)) subtractor_1 (.a(in_1[14:10]), .b(5'b01111), .out(subtractor_1_out));  // open: bin, bout
  Shifter #(.width(32)) shifter_1 (.in(32'h1), .\dist (subtractor_1_out), .out(shifter_1_out));
  Shifter #(.width(32)) shifter_2 (.in({{22{1'b0}}, in_1[9:0]}), .\dist (subtractor_1_out), .out(shifter_2_out));
  Shifter #(.width(32), .shift("lr")) shifter_3 (.in(shifter_2_out), .\dist (5'b01010), .out(shifter_3_out));
  assign or_1_out = shifter_1_out | shifter_3_out;  // OR_Gate or_1, 32 bits wide
  Comparator #(.width(5), .mode("unsigned")) comparator_1 (
    .a({5{1'b1}}), .b(in_1[14:10]), .eq(comparator_1_eq));  // open: gt, lt
  Comparator #(.width(5), .mode("unsigned")) comparator_2 (
    .a(5'b01111), .b(in_1[14:10]), .gt(comparator_2_gt));  // open: eq, lt
  neg neg_1 (.in_1(or_1_out), .in_2(in_1[15]), .out_3(neg_1_out_3));
  or or_2 (or_2_out, comparator_1_eq, comparator_2_gt);
  Multiplexer #(.width(32)) multiplexer_1 (
    .in0(neg_1_out_3), .in1({32{1'b0}}), .out(out_2), .sel(or_2_out));  // open: en

  // Other names for the same wires on the sheet: frac[9:0] = in_1[9:0]; exp[4:0] = in_1[14:10]; sign = in_1[15]
endmodule

module neg (
  input  [31:0] in_1,
  input  in_2,
  output [31:0] out_3
);

  wire [31:0] adder_1_out, xor_1_out;

  assign xor_1_out = in_1 ^ {32{1'b1}};  // XOR_Gate xor_1, 32 bits wide
  Adder #(.width(32)) adder_1 (.a(xor_1_out), .b(32'h1), .out(adder_1_out));  // open: cin, cout
  Multiplexer #(.width(32)) multiplexer_1 (.in0(in_1), .in1(adder_1_out), .out(out_3), .sel(in_2));  // open: en
endmodule
