// Logisim project navigation.circ as structural Verilog
module navigation (
  input  [1:0] dir,
  input  clk,
  input  reset,
  output arrive,
  output hit
);

  wire comparator_1_eq, move_1_hit;
  wire [2:0] move_1_out_4, register_3_q;

  move move_1 (.in_1(dir), .in_2(register_3_q), .hit(move_1_hit), .out_4(move_1_out_4));
  Comparator #(.width(3)) comparator_1 (.a(3'b100), .b(move_1_out_4), .eq(comparator_1_eq));  // open: gt, lt
  Register #(.width(1)) register_1 (.D(comparator_1_eq), .Q(arrive), .clk(clk), .clr(reset));  // open: en
  Register #(.width(1)) register_2 (.D(move_1_hit), .Q(hit), .clk(clk), .clr(reset));  // open: en
  Register #(.width(3)) register_3 (.D(move_1_out_4), .Q(register_3_q), .clk(clk), .clr(reset));  // open: en
endmodule

module move (
  input  [1:0] in_1,
  input  [2:0] in_2,
  output hit,
  output [2:0] out_4
);

  wire [3:0] multiplexer_1_out, multiplexer_2_out, multiplexer_3_out, multiplexer_4_out;

  Multiplexer #(.select(2), .width(4), .enable("false")) multiplexer_1 (
    .in0(4'b0001), .in1(4'b1000), .in2(4'b1000), .in3(4'b1000), .out(multiplexer_1_out), .sel(in_1));
  Multiplexer #(.select(2), .width(4), .enable("false")) multiplexer_2 (
    .in0(4'b0010), .in1(4'b0011), .in2(4'b0000), .in3(4'b1001), .out(multiplexer_2_out), .sel(in_1));
  Multiplexer #(.select(2), .width(4), .enable("false")) multiplexer_3 (
    .in0(4'b1010), .in1(4'b0100), .in2(4'b0001), .in3(4'b1010), .out(multiplexer_3_out), .sel(in_1));
  Multiplexer #(.select(2), .width(4), .enable("false")) multiplexer_4 (
    .in0(4'b0100), .in1(4'b1011), .in2(4'b1011), .in3(4'b0001), .out(multiplexer_4_out), .sel(in_1));
  Multiplexer #(.select(3), .width(4), .enable("false")) multiplexer_5 (
    .in0(multiplexer_1_out), .in1(multiplexer_2_out), .in2(multiplexer_3_out), .in3(multiplexer_4_out),
    .in4(4'b0000), .in5(4'b0000), .in6(4'b0000), .in7(4'b0000), .out({hit, out_4}), .sel(in_2));
endmodule
