// Logisim project 1.circ as structural Verilog: 12 circuits, main circuit main
module main (
  input  in_1,
  output [31:0] out_2,
  output out_3,
  output [4:0] out_4,
  output [31:0] out_5,
  output out_6,
  output [4:0] out_7,
  output [31:0] out_8
);

  wire alu_1_zero, ALUSrc, Branch, Clk, ImmSign, MemtoReg, PCSrc, RegDst;
  wire [2:0] ALUControl;
  wire [31:0] ALUResult, bit_extender_1_out, bit_extender_2_out, dm_1_rd, grf_1_rd1, multiplexer_1_out,
       multiplexer_3_out, multiplexer_4_out, Offset;

  Clock clock_1 (.out(Clk));
  Multiplexer #(.width(32)) multiplexer_1 (
    .in0({32{1'b0}}), .in1(Offset), .out(multiplexer_1_out), .sel(PCSrc));  // open: en
  Multiplexer #(.width(5)) multiplexer_2 (
    .in0(out_2[15:11]), .in1(out_2[20:16]), .out(out_4), .sel(RegDst));  // open: en
  assign bit_extender_1_out = {{16{1'b0}}, out_2[15:0]};  // Bit_Extender bit_extender_1
  assign bit_extender_2_out = {{16{out_2[15]}}, out_2[15:0]};  // Bit_Extender bit_extender_2
  IFU ifu_1 (.Offset(multiplexer_1_out), .out_4(out_2), .Clk(Clk), .Reset(in_1));
  GRF grf_1 (
    .A1(out_2[25:21]), .A2(out_2[20:16]), .A3(out_4), .WD(out_5), .RD1(grf_1_rd1), .RD2(out_8), .Clk(Clk),
    .Reset(in_1), .WE(out_3));
  Multiplexer #(.width(32)) multiplexer_3 (
    .in0(bit_extender_1_out), .in1(bit_extender_2_out), .out(multiplexer_3_out), .sel(ImmSign));  // open: en
  Multiplexer #(.width(32)) multiplexer_4 (
    .in0(out_8), .in1(multiplexer_3_out), .out(multiplexer_4_out), .sel(ALUSrc));  // open: en
  Shifter #(.width(32)) shifter_1 (.in(bit_extender_2_out), .\dist (5'b00010), .out(Offset));
  ALU alu_1 (
    .SrcA(grf_1_rd1), .SrcB(multiplexer_4_out), .Zero(alu_1_zero),
    .ALUResult({ALUResult[31:7], out_7, ALUResult[1:0]}), .ALUOp(ALUControl));
  Controller controller_1 (
    .Op(out_2[31:26]), .Funct(out_2[5:0]), .MemtoReg(MemtoReg), .MemWrite(out_6), .Branch(Branch),
    .ALUControl(ALUControl), .ALUSrc(ALUSrc), .RegDst(RegDst), .RegWrite(out_3), .ImmSign(ImmSign));
  and and_1 (PCSrc, Branch, alu_1_zero);
  DM dm_1 (.Clk(Clk), .WE(out_6), .RD(dm_1_rd), .A({ALUResult[31:7], out_7, ALUResult[1:0]}), .WD(out_8), .Reset(in_1));
  Multiplexer #(.width(32)) multiplexer_5 (
    .in0({ALUResult[31:7], out_7, ALUResult[1:0]}), .in1(dm_1_rd), .out(out_5), .sel(MemtoReg));  // open: en

  // Other names for the same wires on the sheet: ALUResult[6:2] = out_7; MemAddr[4:0] = out_7;
  //   Addr[25:0] = out_2[25:0]; Funct[5:0] = out_2[5:0]; Imm[15:0] = out_2[15:0]; Instr[31:0] = out_2;
  //   Shamt[4:0] = out_2[10:6]; Rd[4:0] = out_2[15:11]; Rt[4:0] = out_2[20:16]; Rs[4:0] = out_2[25:21];
  //   Op[5:0] = out_2[31:26]; MemData[31:0] = out_8; MemWrite = out_6; RegAddr[4:0] = out_4; RegData[31:0] = out_5;
  //   RegWrite = out_3; Reset = in_1
endmodule

module GRF_L0 (
  input  in_1,
  input  in_2,
  input  in_3,
  input  [31:0] in_4,
  output [31:0] out_5
);

  Register #(.width(32)) register_1 (.D(in_4), .en(in_2), .Q(out_5), .clk(in_1), .clr(in_3));
endmodule

module GRF_L1 (
  input  in_1,
  input  in_2,
  input  in_3,
  input  in_4,
  input  in_5,
  input  in_6,
  input  [31:0] in_7,
  output [31:0] out_8,
  output [31:0] out_9
);

  wire E0, E1, not_1_out;
  wire [31:0] grf_l0_1_out_5, grf_l0_2_out_5;

  not not_1 (not_1_out, in_4);
  GRF_L0 grf_l0_1 (.in_4(in_7), .out_5(grf_l0_1_out_5), .in_1(in_5), .in_2(E0), .in_3(in_6));
  GRF_L0 grf_l0_2 (.in_4(in_7), .out_5(grf_l0_2_out_5), .in_1(in_5), .in_2(E1), .in_3(in_6));
  and and_1 (E0, in_1, not_1_out);
  and and_2 (E1, in_1, in_4);
  Multiplexer #(.width(32)) multiplexer_1 (
    .in0(grf_l0_1_out_5), .in1(grf_l0_2_out_5), .out(out_8), .sel(in_2));  // open: en
  Multiplexer #(.width(32)) multiplexer_2 (
    .in0(grf_l0_1_out_5), .in1(grf_l0_2_out_5), .out(out_9), .sel(in_3));  // open: en

  // Other names for the same wires on the sheet: S1 = in_2; S2 = in_3
endmodule

module GRF_L2 (
  input  [1:0] in_1,
  input  in_2,
  input  [1:0] in_3,
  input  [1:0] in_4,
  input  in_5,
  input  in_6,
  input  [31:0] in_7,
  output [31:0] out_8,
  output [31:0] out_9
);

  wire E0, E1, not_1_out;
  wire [31:0] grf_l1_1_out_8, grf_l1_1_out_9, grf_l1_2_out_8, grf_l1_2_out_9;

  and and_1 (E0, in_2, not_1_out);
  not not_1 (not_1_out, in_4[1]);
  and and_2 (E1, in_2, in_4[1]);
  GRF_L1 grf_l1_1 (
    .in_2(in_1[0]), .in_3(in_3[0]), .in_4(in_4[0]), .in_7(in_7), .out_8(grf_l1_1_out_8),
    .out_9(grf_l1_1_out_9), .in_5(in_5), .in_1(E0), .in_6(in_6));
  GRF_L1 grf_l1_2 (
    .in_2(in_1[0]), .in_3(in_3[0]), .in_4(in_4[0]), .in_7(in_7), .out_8(grf_l1_2_out_8),
    .out_9(grf_l1_2_out_9), .in_5(in_5), .in_1(E1), .in_6(in_6));
  Multiplexer #(.width(32)) multiplexer_1 (
    .in0(grf_l1_1_out_8), .in1(grf_l1_2_out_8), .out(out_8), .sel(in_1[1]));  // open: en
  Multiplexer #(.width(32)) multiplexer_2 (
    .in0(grf_l1_1_out_9), .in1(grf_l1_2_out_9), .out(out_9), .sel(in_3[1]));  // open: en

  // Other names for the same wires on the sheet: T1 = in_1[0]; S1 = in_1[1]; T2 = in_3[0]; S2 = in_3[1]; T3 = in_4[0]
endmodule

module GRF_L3 (
  input  [2:0] in_1,
  input  in_2,
  input  [2:0] in_3,
  input  [2:0] in_4,
  input  in_5,
  input  in_6,
  input  [31:0] in_7,
  output [31:0] out_8,
  output [31:0] out_9
);

  wire E0, E1, not_1_out;
  wire [31:0] grf_l2_1_out_8, grf_l2_1_out_9, grf_l2_2_out_8, grf_l2_2_out_9;

  and and_1 (E0, in_2, not_1_out);
  not not_1 (not_1_out, in_4[2]);
  and and_2 (E1, in_2, in_4[2]);
  GRF_L2 grf_l2_1 (
    .in_1(in_1[1:0]), .in_3(in_3[1:0]), .in_4(in_4[1:0]), .in_7(in_7), .out_8(grf_l2_1_out_8),
    .out_9(grf_l2_1_out_9), .in_5(in_5), .in_2(E0), .in_6(in_6));
  GRF_L2 grf_l2_2 (
    .in_1(in_1[1:0]), .in_3(in_3[1:0]), .in_4(in_4[1:0]), .in_7(in_7), .out_8(grf_l2_2_out_8),
    .out_9(grf_l2_2_out_9), .in_5(in_5), .in_2(E1), .in_6(in_6));
  Multiplexer #(.width(32)) multiplexer_1 (
    .in0(grf_l2_1_out_8), .in1(grf_l2_2_out_8), .out(out_8), .sel(in_1[2]));  // open: en
  Multiplexer #(.width(32)) multiplexer_2 (
    .in0(grf_l2_1_out_9), .in1(grf_l2_2_out_9), .out(out_9), .sel(in_3[2]));  // open: en

  // Other names for the same wires on the sheet: T1[1:0] = in_1[1:0]; S1 = in_1[2]; T2[1:0] = in_3[1:0]; S2 = in_3[2];
  //   T3[1:0] = in_4[1:0]
endmodule

module GRF_L4 (
  input  [3:0] in_1,
  input  in_2,
  input  [3:0] in_3,
  input  [3:0] in_4,
  input  in_5,
  input  in_6,
  input  [31:0] in_7,
  output [31:0] out_8,
  output [31:0] out_9
);

  wire E0, E1, not_1_out;
  wire [31:0] grf_l3_1_out_8, grf_l3_1_out_9, grf_l3_2_out_8, grf_l3_2_out_9;

  and and_1 (E0, in_2, not_1_out);
  not not_1 (not_1_out, in_4[3]);
  and and_2 (E1, in_2, in_4[3]);
  GRF_L3 grf_l3_1 (
    .in_1(in_1[2:0]), .in_3(in_3[2:0]), .in_4(in_4[2:0]), .in_7(in_7), .out_8(grf_l3_1_out_8),
    .out_9(grf_l3_1_out_9), .in_5(in_5), .in_2(E0), .in_6(in_6));
  GRF_L3 grf_l3_2 (
    .in_1(in_1[2:0]), .in_3(in_3[2:0]), .in_4(in_4[2:0]), .in_7(in_7), .out_8(grf_l3_2_out_8),
    .out_9(grf_l3_2_out_9), .in_5(in_5), .in_2(E1), .in_6(in_6));
  Multiplexer #(.width(32)) multiplexer_1 (
    .in0(grf_l3_1_out_8), .in1(grf_l3_2_out_8), .out(out_8), .sel(in_1[3]));  // open: en
  Multiplexer #(.width(32)) multiplexer_2 (
    .in0(grf_l3_1_out_9), .in1(grf_l3_2_out_9), .out(out_9), .sel(in_3[3]));  // open: en

  // Other names for the same wires on the sheet: T1[2:0] = in_1[2:0]; S1 = in_1[3]; T2[2:0] = in_3[2:0]; S2 = in_3[3];
  //   T3[2:0] = in_4[2:0]
endmodule

module GRF_L5 (
  input  [4:0] in_1,
  input  in_2,
  input  [4:0] in_3,
  input  [4:0] in_4,
  input  in_5,
  input  in_6,
  input  [31:0] in_7,
  output [31:0] out_8,
  output [31:0] out_9
);

  wire E0, E1, not_1_out;
  wire [31:0] grf_l4_1_out_8, grf_l4_1_out_9, grf_l4_2_out_8, grf_l4_2_out_9;

  and and_1 (E0, in_2, not_1_out);
  not not_1 (not_1_out, in_4[4]);
  and and_2 (E1, in_2, in_4[4]);
  GRF_L4 grf_l4_1 (
    .in_1(in_1[3:0]), .in_3(in_3[3:0]), .in_4(in_4[3:0]), .in_7(in_7), .out_8(grf_l4_1_out_8),
    .out_9(grf_l4_1_out_9), .in_5(in_5), .in_2(E0), .in_6(in_6));
  GRF_L4 grf_l4_2 (
    .in_1(in_1[3:0]), .in_3(in_3[3:0]), .in_4(in_4[3:0]), .in_7(in_7), .out_8(grf_l4_2_out_8),
    .out_9(grf_l4_2_out_9), .in_5(in_5), .in_2(E1), .in_6(in_6));
  Multiplexer #(.width(32)) multiplexer_1 (
    .in0(grf_l4_1_out_8), .in1(grf_l4_2_out_8), .out(out_8), .sel(in_1[4]));  // open: en
  Multiplexer #(.width(32)) multiplexer_2 (
    .in0(grf_l4_1_out_9), .in1(grf_l4_2_out_9), .out(out_9), .sel(in_3[4]));  // open: en

  // Other names for the same wires on the sheet: T1[3:0] = in_1[3:0]; S1 = in_1[4]; T2[3:0] = in_3[3:0]; S2 = in_3[4];
  //   T3[3:0] = in_4[3:0]
endmodule

module GRF (
  input  Clk,
  input  Reset,
  input  WE,
  input  [4:0] A1,
  input  [4:0] A2,
  input  [4:0] A3,
  input  [31:0] WD,
  output [31:0] RD1,
  output [31:0] RD2
);

  wire comparator_1_eq;
  wire [31:0] multiplexer_1_out;

  Comparator #(.width(5)) comparator_1 (.a(A3), .b({5{1'b0}}), .eq(comparator_1_eq));  // open: gt, lt
  Multiplexer #(.width(32)) multiplexer_1 (
    .in0(WD), .in1({32{1'b0}}), .out(multiplexer_1_out), .sel(comparator_1_eq));  // open: en
  GRF_L5 grf_l5_1 (
    .in_1(A1), .in_3(A2), .in_4(A3), .in_7(multiplexer_1_out), .out_8(RD1), .out_9(RD2), .in_5(Clk),
    .in_2(WE), .in_6(Reset));
endmodule

module ALU (
  input  [2:0] ALUOp,
  input  [31:0] SrcA,
  input  [31:0] SrcB,
  output Zero,
  output [31:0] ALUResult
);

  wire [31:0] r0, r1, r2, r3;

  Adder #(.width(32)) adder_1 (.a(SrcA), .b(SrcB), .out(r0));  // open: cin, cout
  Subtractor #(.width(32)) subtractor_1 (.a(SrcA), .b(SrcB), .out(r1));  // open: bin, bout
  assign r2 = SrcA | SrcB;  // OR_Gate or_1, 32 bits wide
  Shifter #(.width(32)) shifter_1 (.in(SrcB), .\dist (5'b10000), .out(r3));
  Multiplexer #(.select(3), .width(32)) multiplexer_1 (
    .in0(r0), .in1(r1), .in2(r2), .in3(r3), .in4({32{1'b0}}), .in5({32{1'b0}}), .in6({32{1'b0}}),
    .in7({32{1'b0}}), .out(ALUResult), .sel(ALUOp));  // open: en
  Comparator #(.width(32)) comparator_1 (.a({32{1'b0}}), .b(ALUResult), .eq(Zero));  // open: gt, lt
endmodule

module IFU (
  input  Clk,
  input  Reset,
  input  [31:0] Offset,
  output [31:0] out_4
);

  wire [31:0] adder_1_out, adder_2_out, register_1_q;

  Adder #(.width(32)) adder_1 (.a(32'h4), .b(register_1_q), .out(adder_1_out));  // open: cin, cout
  Adder #(.width(32)) adder_2 (.a(Offset), .b(adder_1_out), .out(adder_2_out));  // open: cin, cout
  Register #(.width(32)) register_1 (.D(adder_2_out), .Q(register_1_q), .clk(Clk), .clr(Reset));  // open: en
  ROM #(.addrWidth(5), .dataWidth(32)) rom_1 (.addr(register_1_q[6:2]), .data(out_4));  // open: sel

  // Notes on the sheet:
  //   contents of rom_1 (hex, n*v repeats v):
  //   3c010064 34020064 340300c8 822021 ac040000 8c050000 10640001 1085fff8
endmodule

module DM (
  input  Clk,
  input  Reset,
  input  WE,
  input  [31:0] A,
  input  [31:0] WD,
  output [31:0] RD
);

  RAM #(.addrWidth(5), .dataWidth(32), .bus("separate")) ram_1 (
    .addr(A[6:2]), .din(WD), .data(RD), .str(WE), .clk(Clk), .ld(1'b1), .clr(Reset));  // open: sel
endmodule

module Controller (
  input  [5:0] Op,
  input  [5:0] Funct,
  output MemtoReg,
  output MemWrite,
  output Branch,
  output [2:0] ALUControl,
  output ALUSrc,
  output RegDst,
  output RegWrite,
  output ImmSign
);

  wire addu, beq, FnZ, lui, lw, nop, OpZ, ori, subu, sw;

  Comparator #(.width(6)) comparator_1 (.a(Op), .b({6{1'b0}}), .eq(OpZ));  // open: gt, lt
  Comparator #(.width(6)) comparator_2 (.a(Funct), .b({6{1'b0}}), .eq(FnZ));  // open: gt, lt
  and u_addu (addu, OpZ, Funct[5], ~Funct[4], ~Funct[3], ~Funct[2], ~Funct[1], Funct[0]);  // AND_Gate
  and u_subu (subu, OpZ, Funct[5], ~Funct[4], ~Funct[3], ~Funct[2], Funct[1], Funct[0]);  // AND_Gate
  and u_ori (ori, ~Op[5], ~Op[4], Op[3], Op[2], ~Op[1], Op[0]);  // AND_Gate
  and u_lw (lw, Op[5], ~Op[4], ~Op[3], ~Op[2], Op[1], Op[0]);  // AND_Gate
  and u_sw (sw, Op[5], ~Op[4], Op[3], ~Op[2], Op[1], Op[0]);  // AND_Gate
  and u_beq (beq, ~Op[5], ~Op[4], ~Op[3], Op[2], ~Op[1], ~Op[0]);  // AND_Gate
  and u_lui (lui, ~Op[5], ~Op[4], Op[3], Op[2], Op[1], Op[0]);  // AND_Gate
  and u_nop (nop, OpZ, FnZ);
  buf or_1 (MemtoReg, lw);  // OR_Gate
  buf or_2 (MemWrite, sw);  // OR_Gate
  buf or_3 (Branch, beq);  // OR_Gate
  or or_4 (ALUControl[0], subu, beq, lui);
  or or_5 (ALUControl[1], ori, lui);
  or or_6 (ALUSrc, ori, lw, sw, lui);
  or or_7 (RegDst, ori, lw, lui);
  or or_8 (RegWrite, addu, subu, ori, lw, lui);
  or or_9 (ImmSign, lw, sw, beq);

  assign ALUControl[2] = 1'b0;

  // Other names for the same wires on the sheet: Fn0 = Funct[0]; Fn1 = Funct[1]; Fn2 = Funct[2]; Fn3 = Funct[3];
  //   Fn4 = Funct[4]; Fn5 = Funct[5]
endmodule
