// Logisim project 4BitSort.circ as structural Verilog
module _1bit_swap (
  input  I1,
  input  I2,
  input  S,
  output O1,
  output O2
);

  wire and_1_out, and_2_out, and_3_out, and_4_out, S_0;

  not not_1 (S_0, S);
  and and_1 (and_1_out, I1, S_0);
  and and_2 (and_2_out, I2, S);
  and and_3 (and_3_out, I1, S);
  and and_4 (and_4_out, I2, S_0);
  or or_1 (O1, and_1_out, and_2_out);
  or or_2 (O2, and_3_out, and_4_out);

  // Other names for the same wires on the sheet: S_1 = S
endmodule

module _4bit_swap (
  input  [3:0] I1,
  input  [3:0] I2,
  input  S,
  output [3:0] O1,
  output [3:0] O2
);

  _1bit_swap u_1bit_swap_1 (.I1(I1[0]), .I2(I2[0]), .S(S), .O1(O1[0]), .O2(O2[0]));
  _1bit_swap u_1bit_swap_2 (.I1(I1[1]), .I2(I2[1]), .S(S), .O1(O1[1]), .O2(O2[1]));
  _1bit_swap u_1bit_swap_3 (.I1(I1[2]), .I2(I2[2]), .S(S), .O1(O1[2]), .O2(O2[2]));
  _1bit_swap u_1bit_swap_4 (.I1(I1[3]), .I2(I2[3]), .S(S), .O1(O1[3]), .O2(O2[3]));

  // Other names for the same wires on the sheet: A_0 = I1[0]; A_1 = I1[1]; A_2 = I1[2]; A_3 = I1[3]; B_0 = I2[0];
  //   B_1 = I2[1]; B_2 = I2[2]; B_3 = I2[3]
endmodule

module _4bit_sort (
  input  [3:0] A,
  input  [3:0] B,
  input  [3:0] C,
  input  [3:0] D,
  output [3:0] _1,
  output [3:0] _2,
  output [3:0] _3,
  output [3:0] _4
);

  wire [3:0] n4bit_sort_2num_1_o1, n4bit_sort_2num_1_o2, n4bit_sort_2num_2_o2, n4bit_sort_2num_3_o1,
       n4bit_sort_2num_3_o2, n4bit_sort_2num_4_o1, n4bit_sort_2num_4_o2, n4bit_sort_2num_5_o2;

  _4bit_sort_2num u_4bit_sort_2num_1 (.I1(C), .I2(D), .O1(n4bit_sort_2num_1_o1), .O2(n4bit_sort_2num_1_o2));
  _4bit_sort_2num u_4bit_sort_2num_2 (.I1(A), .I2(n4bit_sort_2num_3_o1), .O1(_1), .O2(n4bit_sort_2num_2_o2));
  _4bit_sort_2num u_4bit_sort_2num_3 (
    .I1(B), .I2(n4bit_sort_2num_1_o1), .O1(n4bit_sort_2num_3_o1), .O2(n4bit_sort_2num_3_o2));
  _4bit_sort_2num u_4bit_sort_2num_4 (
    .I1(n4bit_sort_2num_3_o2), .I2(n4bit_sort_2num_1_o2), .O1(n4bit_sort_2num_4_o1), .O2(n4bit_sort_2num_4_o2));
  _4bit_sort_2num u_4bit_sort_2num_5 (
    .I1(n4bit_sort_2num_2_o2), .I2(n4bit_sort_2num_4_o1), .O1(_2), .O2(n4bit_sort_2num_5_o2));
  _4bit_sort_2num u_4bit_sort_2num_6 (.I1(n4bit_sort_2num_5_o2), .I2(n4bit_sort_2num_4_o2), .O1(_3), .O2(_4));
endmodule

module _4bit_sort_2num (
  input  [3:0] I1,
  input  [3:0] I2,
  output [3:0] O1,
  output [3:0] O2
);

  wire comparator_1_gt;

  _4bit_swap u_4bit_swap_1 (.I1(I1), .I2(I2), .S(comparator_1_gt), .O1(O1), .O2(O2));
  Comparator #(.width(4), .mode("unsigned")) comparator_1 (.a(I1), .b(I2), .gt(comparator_1_gt));  // open: eq, lt
endmodule
