// Logisim project Logisim_mod5.circ as structural Verilog: 1 circuit, main circuit mod5
module mod5 (
  input  in_1,
  output out_2,
  output out_3,
  output out_4,
  output out_5,
  output out_6
);

  wire and_1_out, and_2_out, and_3_out, and_4_out, and_5_out, and_6_out, and_7_out, and_8_out, clock_1_out,
       clock_2_out, clock_3_out, clock_4_out, clock_5_out, multiplexer_1_out, not_1_out, not_2_out,
       not_3_out, not_4_out, not_5_out, register_1_q, register_2_q, register_3_q, register_4_q, register_5_q;

  Clock clock_1 (.out(clock_1_out));
  Clock clock_2 (.out(clock_2_out));
  Clock clock_3 (.out(clock_3_out));
  Clock clock_4 (.out(clock_4_out));
  Register #(.width(1)) register_1 (.D(out_3), .Q(register_1_q), .clk(clock_1_out));  // open: en, clr
  Register #(.width(1)) register_2 (.D(out_4), .Q(register_2_q), .clk(clock_2_out));  // open: en, clr
  Register #(.width(1)) register_3 (.D(out_6), .Q(register_3_q), .clk(clock_3_out));  // open: en, clr
  Register #(.width(1)) register_4 (.D(out_5), .Q(register_4_q), .clk(clock_4_out));  // open: en, clr
  not not_1 (not_1_out, in_1);
  not not_2 (not_2_out, in_1);
  not not_3 (not_3_out, in_1);
  not not_4 (not_4_out, in_1);
  and and_1 (and_1_out, not_1_out, register_3_q);
  and and_2 (and_2_out, register_1_q, not_2_out);
  and and_3 (and_3_out, register_1_q, in_1);
  and and_4 (and_4_out, register_3_q, in_1);
  and and_5 (and_5_out, register_2_q, not_3_out);
  and and_6 (and_6_out, not_4_out, register_4_q);
  and and_7 (and_7_out, register_2_q, in_1);
  and and_8 (and_8_out, register_4_q, in_1);
  or or_1 (out_4, and_3_out, and_4_out);
  or or_2 (out_6, and_5_out, and_6_out);
  or or_3 (out_5, and_7_out, and_8_out);
  not not_5 (not_5_out, register_5_q);
  Multiplexer multiplexer_1 (.in0(1'b1), .in1(1'b0), .out(multiplexer_1_out), .sel(register_5_q));  // open: en
  Register #(.width(1)) register_5 (.D(not_5_out), .en(not_5_out), .Q(register_5_q), .clk(clock_5_out));  // open: clr
  Clock clock_5 (.out(clock_5_out));
  or or_4 (out_3, and_1_out, and_2_out, multiplexer_1_out);

  assign out_2 = 1'b0;
endmodule
