// Logisim project fib.circ as structural Verilog: 4 circuits, main circuit main
module main (
  input  [2:0] in_1,
  output [31:0] out_2
);

  wire clock_1_out, counter_1_q, get_1_out_2, get_1_out_3;
  wire [31:0] adder_1_out, adder_2_out, matrix_1_out_2, matrix_1_out_3, matrix_1_out_4, matrix_1_out_5,
       multiplexer_1_out, multiplexer_2_out, multiplier_1_out, multiplier_2_out, multiplier_3_out,
       multiplier_4_out, register_1_q, register_2_q;

  get get_1 (.in_1(in_1), .out_2(get_1_out_2), .out_3(get_1_out_3));
  matrix matrix_1 (
    .in_1(get_1_out_2), .out_2(matrix_1_out_2), .out_3(matrix_1_out_3), .out_4(matrix_1_out_4),
    .out_5(matrix_1_out_5));
  Multiplexer #(.width(32)) multiplexer_1 (
    .in0(32'h1), .in1(adder_1_out), .out(multiplexer_1_out), .sel(counter_1_q));  // open: en
  Multiplexer #(.width(32)) multiplexer_2 (
    .in0({32{1'b0}}), .in1(adder_2_out), .out(multiplexer_2_out), .sel(counter_1_q));  // open: en
  Counter #(.width(1), .max('h1), .ongoal("stay")) counter_1 (
    .Q(counter_1_q), .clk(clock_1_out));  // open: load, D, count, carry, clr
  Register #(.width(32)) register_1 (.D(multiplexer_1_out), .Q(register_1_q), .clk(clock_1_out));  // open: en, clr
  Register #(.width(32)) register_2 (.D(multiplexer_2_out), .Q(register_2_q), .clk(clock_1_out));  // open: en, clr
  Clock clock_1 (.out(clock_1_out));
  Multiplier #(.width(32)) multiplier_1 (
    .a(matrix_1_out_2), .b(register_1_q), .out(multiplier_1_out));  // open: cin, cout
  Multiplier #(.width(32)) multiplier_2 (
    .a(matrix_1_out_4), .b(register_2_q), .out(multiplier_2_out));  // open: cin, cout
  Multiplier #(.width(32)) multiplier_3 (
    .a(matrix_1_out_3), .b(register_1_q), .out(multiplier_3_out));  // open: cin, cout
  Multiplier #(.width(32)) multiplier_4 (
    .a(matrix_1_out_5), .b(register_2_q), .out(multiplier_4_out));  // open: cin, cout
  Adder #(.width(32)) adder_1 (.a(multiplier_1_out), .b(multiplier_2_out), .out(adder_1_out));  // open: cin, cout
  Adder #(.width(32)) adder_2 (.a(multiplier_3_out), .b(multiplier_4_out), .out(adder_2_out));  // open: cin, cout
  Multiplexer #(.width(32)) multiplexer_3 (
    .in0({32{1'b0}}), .in1(multiplexer_2_out), .out(out_2), .sel(get_1_out_3));  // open: en
endmodule

module get (
  input  [2:0] in_1,
  output out_2,
  output out_3
);

  wire clock_1_out, comparator_1_eq, counter_1_q;
  wire [2:0] register_1_q;
  wire [2:1] multiplexer_1_out;

  Multiplexer #(.width(3)) multiplexer_1 (
    .in0(in_1), .in1(register_1_q), .out({multiplexer_1_out, out_2}), .sel(counter_1_q));  // open: en
  Counter #(.width(1), .max('h1), .ongoal("stay")) counter_1 (
    .Q(counter_1_q), .clk(clock_1_out));  // open: load, D, count, carry, clr
  Clock clock_1 (.out(clock_1_out));
  Register #(.width(3)) register_1 (
    .D({1'b0, multiplexer_1_out}), .Q(register_1_q), .clk(clock_1_out));  // open: en, clr
  Comparator #(.width(2)) comparator_1 (.a(multiplexer_1_out), .b(2'b00), .eq(comparator_1_eq));  // open: gt, lt
  Register #(.width(1)) register_2 (.D(comparator_1_eq), .Q(out_3), .clk(clock_1_out));  // open: en, clr
endmodule

module matrix (
  input  in_1,
  output [31:0] out_2,
  output [31:0] out_3,
  output [31:0] out_4,
  output [31:0] out_5
);

  wire clock_1_out, counter_1_q;
  wire [31:0] mat_mul_1_out_5, mat_mul_1_out_6, mat_mul_1_out_7, mat_mul_1_out_8, multiplexer_1_out,
       multiplexer_2_out, multiplexer_3_out, multiplexer_4_out, register_1_q, register_2_q, register_3_q,
       register_4_q;

  Multiplexer #(.width(32)) multiplexer_1 (
    .in0(32'h1), .in1(mat_mul_1_out_5), .out(multiplexer_1_out), .sel(counter_1_q));  // open: en
  Register #(.width(32)) register_1 (.D(multiplexer_1_out), .Q(register_1_q), .clk(clock_1_out));  // open: en, clr
  Multiplexer #(.width(32)) multiplexer_2 (
    .in0(32'h1), .in1(mat_mul_1_out_6), .out(multiplexer_2_out), .sel(counter_1_q));  // open: en
  Register #(.width(32)) register_2 (.D(multiplexer_2_out), .Q(register_2_q), .clk(clock_1_out));  // open: en, clr
  Multiplexer #(.width(32)) multiplexer_3 (
    .in0(32'h1), .in1(mat_mul_1_out_7), .out(multiplexer_3_out), .sel(counter_1_q));  // open: en
  Register #(.width(32)) register_3 (.D(multiplexer_3_out), .Q(register_3_q), .clk(clock_1_out));  // open: en, clr
  Multiplexer #(.width(32)) multiplexer_4 (
    .in0({32{1'b0}}), .in1(mat_mul_1_out_8), .out(multiplexer_4_out), .sel(counter_1_q));  // open: en
  Register #(.width(32)) register_4 (.D(multiplexer_4_out), .Q(register_4_q), .clk(clock_1_out));  // open: en, clr
  Counter #(.width(1), .max('h1), .ongoal("stay")) counter_1 (
    .Q(counter_1_q), .clk(clock_1_out));  // open: load, D, count, carry, clr
  Clock clock_1 (.out(clock_1_out));
  mat_mul mat_mul_1 (
    .in_1(register_1_q), .in_2(register_2_q), .in_3(register_3_q), .in_4(register_4_q),
    .out_5(mat_mul_1_out_5), .out_6(mat_mul_1_out_6), .out_7(mat_mul_1_out_7), .out_8(mat_mul_1_out_8));
  Multiplexer #(.width(32)) multiplexer_5 (.in0(32'h1), .in1(multiplexer_1_out), .out(out_2), .sel(in_1));  // open: en
  Multiplexer #(.width(32)) multiplexer_6 (
    .in0({32{1'b0}}), .in1(multiplexer_2_out), .out(out_3), .sel(in_1));  // open: en
  Multiplexer #(.width(32)) multiplexer_7 (
    .in0({32{1'b0}}), .in1(multiplexer_3_out), .out(out_4), .sel(in_1));  // open: en
  Multiplexer #(.width(32)) multiplexer_8 (.in0(32'h1), .in1(multiplexer_4_out), .out(out_5), .sel(in_1));  // open: en
endmodule

module mat_mul (
  input  [31:0] in_1,
  input  [31:0] in_2,
  input  [31:0] in_3,
  input  [31:0] in_4,
  output [31:0] out_5,
  output [31:0] out_6,
  output [31:0] out_7,
  output [31:0] out_8
);

  wire [31:0] multiplier_1_out, multiplier_2_out, multiplier_3_out, multiplier_4_out, multiplier_5_out,
       multiplier_6_out, multiplier_7_out, multiplier_8_out;

  Multiplier #(.width(32)) multiplier_1 (.a(in_1), .b(in_1), .out(multiplier_1_out));  // open: cin, cout
  Multiplier #(.width(32)) multiplier_2 (.a(in_2), .b(in_2), .out(multiplier_2_out));  // open: cin, cout
  Multiplier #(.width(32)) multiplier_3 (.a(in_1), .b(in_2), .out(multiplier_3_out));  // open: cin, cout
  Multiplier #(.width(32)) multiplier_4 (.a(in_2), .b(in_4), .out(multiplier_4_out));  // open: cin, cout
  Multiplier #(.width(32)) multiplier_5 (.a(in_1), .b(in_3), .out(multiplier_5_out));  // open: cin, cout
  Multiplier #(.width(32)) multiplier_6 (.a(in_3), .b(in_4), .out(multiplier_6_out));  // open: cin, cout
  Multiplier #(.width(32)) multiplier_7 (.a(in_2), .b(in_3), .out(multiplier_7_out));  // open: cin, cout
  Multiplier #(.width(32)) multiplier_8 (.a(in_4), .b(in_4), .out(multiplier_8_out));  // open: cin, cout
  Adder #(.width(32)) adder_1 (.a(multiplier_1_out), .b(multiplier_2_out), .out(out_5));  // open: cin, cout
  Adder #(.width(32)) adder_2 (.a(multiplier_3_out), .b(multiplier_4_out), .out(out_6));  // open: cin, cout
  Adder #(.width(32)) adder_3 (.a(multiplier_5_out), .b(multiplier_6_out), .out(out_7));  // open: cin, cout
  Adder #(.width(32)) adder_4 (.a(multiplier_7_out), .b(multiplier_8_out), .out(out_8));  // open: cin, cout
endmodule
