// Logisim project mod5.circ as structural Verilog
module mod5 (
  input  in_1,
  output S0,
  output S1,
  output S2,
  output S3,
  output S4
);

  wire clock_1_out;
  wire [1:0] register_1_q, run_1_out_3;

  Run run_1 (.in_1(register_1_q), .in_2(in_1), .out_3(run_1_out_3));
  Register #(.width(2)) register_1 (.D(run_1_out_3), .en(1'b1), .Q(register_1_q), .clk(clock_1_out));  // open: clr
  Clock clock_1 (.out(clock_1_out));
  Decoder #(.select(2)) decoder_1 (.out0(S1), .out1(S2), .out2(S3), .out3(S4), .sel(run_1_out_3));  // open: en

  assign S0 = 1'b0;
endmodule

module Run (
  input  [1:0] in_1,
  input  in_2,
  output [1:0] out_3
);

  wire and_1_out, and_2_out, not_1_out, not_2_out;

  xor xor_1 (out_3[1], in_1[0], in_1[1]);
  not not_1 (not_1_out, out_3[1]);
  not not_2 (not_2_out, in_2);
  and and_1 (and_1_out, not_1_out, in_2);
  or or_1 (out_3[0], and_1_out, and_2_out);
  and and_2 (and_2_out, out_3[1], not_2_out);
endmodule
