// Logisim project sort1.circ as structural Verilog
module _1bit_swap (
  input  I1,
  input  I2,
  input  S,
  output O1,
  output O2
);

  wire and_1_out, and_2_out, and_3_out, and_4_out, S_0;

  not not_1 (S_0, S);
  and and_1 (and_1_out, I1, S_0);
  and and_2 (and_2_out, I2, S);
  and and_3 (and_3_out, I1, S);
  and and_4 (and_4_out, I2, S_0);
  or or_1 (O1, and_1_out, and_2_out);
  or or_2 (O2, and_3_out, and_4_out);

  // Other names for the same wires on the sheet: S_1 = S
endmodule

module _4bit_swap (
  input  [3:0] I1,
  input  [3:0] I2,
  input  S,
  output [3:0] O1,
  output [3:0] O2
);

  _1bit_swap u_1bit_swap_1 (.I1(I1[0]), .I2(I2[0]), .S(S), .O1(O1[0]), .O2(O2[0]));
  _1bit_swap u_1bit_swap_2 (.I1(I1[1]), .I2(I2[1]), .S(S), .O1(O1[1]), .O2(O2[1]));
  _1bit_swap u_1bit_swap_3 (.I1(I1[2]), .I2(I2[2]), .S(S), .O1(O1[2]), .O2(O2[2]));
  _1bit_swap u_1bit_swap_4 (.I1(I1[3]), .I2(I2[3]), .S(S), .O1(O1[3]), .O2(O2[3]));

  // Other names for the same wires on the sheet: A_0 = I1[0]; A_1 = I1[1]; A_2 = I1[2]; A_3 = I1[3]; B_0 = I2[0];
  //   B_1 = I2[1]; B_2 = I2[2]; B_3 = I2[3]
endmodule

module _4bit_sort (
  input  [3:0] A,
  input  [3:0] B,
  input  [3:0] C,
  input  [3:0] D
);

  wire comparator_1_lt, comparator_2_lt, comparator_3_lt, comparator_4_lt, comparator_5_lt;
  wire [3:0] n4bit_swap_1_o1, n4bit_swap_2_o1, n4bit_swap_2_o2, n4bit_swap_3_o1, n4bit_swap_3_o2,
       n4bit_swap_4_o1, n4bit_swap_5_o2;

  _4bit_swap u_4bit_swap_1 (.I1(C), .I2(D), .S(comparator_1_lt), .O1(n4bit_swap_1_o1), .O2(n4bit_swap_1_o1));
  Comparator #(.width(4)) comparator_1 (.a(C), .b(D), .lt(comparator_1_lt));  // open: gt, eq
  _4bit_swap u_4bit_swap_2 (
    .I1(B), .I2(n4bit_swap_1_o1), .S(comparator_2_lt), .O1(n4bit_swap_2_o1), .O2(n4bit_swap_2_o2));
  Comparator #(.width(4)) comparator_2 (.a(B), .b(n4bit_swap_1_o1), .lt(comparator_2_lt));  // open: gt, eq
  _4bit_swap u_4bit_swap_3 (
    .I1(A), .I2(n4bit_swap_2_o1), .S(comparator_3_lt), .O1(n4bit_swap_3_o1), .O2(n4bit_swap_3_o2));
  Comparator #(.width(4)) comparator_3 (.a(A), .b(n4bit_swap_2_o1), .lt(comparator_3_lt));  // open: gt, eq
  _4bit_swap u_4bit_swap_4 (
    .I1(n4bit_swap_2_o2), .I2(n4bit_swap_1_o1), .S(comparator_4_lt), .O1(n4bit_swap_4_o1),
    .O2(n4bit_swap_4_o1));
  Comparator #(.width(4)) comparator_4 (
    .a(n4bit_swap_2_o2), .b(n4bit_swap_1_o1), .lt(comparator_4_lt));  // open: gt, eq
  _4bit_swap u_4bit_swap_5 (
    .I1(n4bit_swap_3_o2), .I2(n4bit_swap_4_o1), .S(comparator_5_lt), .O2(n4bit_swap_5_o2));  // open: O1
  Comparator #(.width(4)) comparator_5 (
    .a(n4bit_swap_3_o2), .b(n4bit_swap_4_o1), .lt(comparator_5_lt));  // open: gt, eq
endmodule

module _4bit_sort_2num (
  input  [3:0] I1,
  input  [3:0] I2,
  output [3:0] O1,
  output [3:0] O2
);

  wire comparator_1_lt;

  _4bit_swap u_4bit_swap_1 (.I1(I1), .I2(I2), .S(comparator_1_lt), .O1(O1), .O2(O1));
  Comparator #(.width(4)) comparator_1 (.a(I1), .b(I2), .lt(comparator_1_lt));  // open: gt, eq

  assign O2 = O1;
endmodule
